// Logisim project decodeur.circ as structural Verilog: 1 circuit, main circuit main
module main (
  input  [2:0] in_1,
  output out_2,
  output out_3,
  output out_4,
  output out_5,
  output out_6,
  output out_7,
  output out_8,
  output out_9,
  output out_10,
  output out_11,
  output out_12,
  output [7:0] out_13,
  output [7:0] out_14
);

  wire not_1_out, not_2_out, not_3_out;

  not not_1 (not_1_out, in_1[2]);
  not not_2 (not_2_out, in_1[1]);
  not not_3 (not_3_out, in_1[0]);
  and and_1 (out_6, not_1_out, not_2_out, in_1[0]);
  and and_2 (out_5, not_1_out, not_2_out, not_3_out);
  Decoder #(.select(3)) decoder_1 (
    .out0(out_14[0]), .out1(out_14[1]), .out2(out_14[2]), .out3(out_14[3]), .out4(out_14[4]),
    .out5(out_14[5]), .out6(out_14[6]), .out7(out_14[7]), .sel(in_1));  // open: en
  and and_3 (out_7, not_1_out, in_1[1], not_3_out);
  and and_4 (out_8, not_1_out, in_1[1], in_1[0]);
  and and_5 (out_9, in_1[2], not_2_out, not_3_out);
  and and_6 (out_10, in_1[2], not_2_out, in_1[0]);
  and and_7 (out_11, in_1[2], in_1[1], not_3_out);
  and and_8 (out_12, in_1[2], in_1[1], in_1[0]);

  assign out_2 = in_1[2];
  assign out_3 = in_1[1];
  assign out_4 = in_1[0];
  assign out_13 = {out_12, out_11, out_10, out_9, out_8, out_7, out_6, out_5};
endmodule
