// Logisim project encodeuroctal.circ as structural Verilog: 1 circuit, main circuit main
module main (
  input  [7:0] in_1,
  output [2:0] out_2
);

  or or_1 (out_2[2], in_1[7], in_1[6], in_1[5], in_1[4]);
  or or_2 (out_2[1], in_1[2], in_1[3], in_1[7], in_1[6]);
  or or_3 (out_2[0], in_1[1], in_1[3], in_1[5], in_1[7]);

  // Notes on the sheet:
  //   e0
  //   e7
  //   4567
  //   2367
  //   1357
  //   s0
  //   s1
  //   s2
endmodule
