// Logisim project multiplexeur.circ as structural Verilog: 1 circuit, main circuit main
module main (
  input  [1:0] in_1,
  input  in_2,
  output out_3,
  output out_4
);

  wire and_1_out, and_2_out, not_1_out;

  Multiplexer multiplexer_1 (.in0(in_1[0]), .in1(in_1[1]), .out(out_4), .sel(in_2));  // open: en
  not not_1 (not_1_out, in_2);
  and and_1 (and_1_out, not_1_out, in_1[0]);
  and and_2 (and_2_out, in_2, in_1[1]);
  or or_1 (out_3, and_1_out, and_2_out);
endmodule
