// Logisim project pariteimpaire.circ as structural Verilog: 1 circuit, main circuit main
module main (
  input  [2:0] in_1,
  output out_2
);

  wire xor_1_out;

  xor xor_1 (xor_1_out, in_1[0], in_1[1]);
  xor xor_2 (out_2, xor_1_out, in_1[2]);
endmodule
