// Logisim project tp2_aluetu.circ as structural Verilog: 9 circuits, main circuit ALU
module ALU (
  input  [15:0] Input1,
  input  [15:0] Input2,
  input  [15:0] Cst,
  input  e1,
  input  [1:0] e2,
  output [15:0] Output
);

  wire [15:0] adder_1_out, and_1_out, multiplexer_1_out, not_1_out;

  Multiplexer #(.width(16), .enable("false")) multiplexer_1 (
    .in0(Input2), .in1(Cst), .out(multiplexer_1_out), .sel(e1));
  Adder #(.width(16)) adder_1 (.a(multiplexer_1_out), .b(Input1), .out(adder_1_out));  // open: cin, cout
  assign and_1_out = Input1 & multiplexer_1_out;  // AND_Gate and_1, 16 bits wide
  Multiplexer #(.select(2), .width(16), .enable("false")) multiplexer_2 (
    .in0(adder_1_out), .in1(and_1_out), .in2(not_1_out), .out(Output), .sel(e2));  // open: in3
  assign not_1_out = ~Input1;  // NOT_Gate not_1, 16 bits wide
endmodule

module ALU_test (
  input  e1,
  input  [1:0] e2
);

  wire [15:0] alu_1_output;

  ALU alu_1 (.e1(e1), .e2(e2), .Output(alu_1_output), .Input1(16'h1234), .Input2(16'h4567), .Cst({16{1'b1}}));
  // Probe on alu_1_output

  // Notes on the sheet:
  //   Cst
  //   Input1
  //   Input2
endmodule

module NZP (
  input  [15:0] in_1,
  output [2:0] NZP
);

  or or_1 (NZP[0], in_1[1], in_1[2], in_1[3], in_1[4], in_1[5], in_1[6], in_1[7], in_1[8], in_1[9], in_1[10], in_1[11], in_1[12], in_1[13], in_1[14], in_1[15], in_1[0]);
  nor nor_1 (NZP[1], in_1[0], in_1[1], in_1[2], in_1[3], in_1[4], in_1[5], in_1[6], in_1[7], in_1[9], in_1[10], in_1[11], in_1[12], in_1[13], in_1[14], in_1[15]);

  assign NZP[2] = in_1[15];

  // Notes on the sheet:
  //   RES
endmodule

module Ext8vers16 (
  input  [7:0] in_1,
  input  [7:0] in_2,
  input  [7:0] in_3,
  output [15:0] out_4,
  output [15:0] out_5
);

  assign out_5 = {{8{1'b0}}, in_3};  // Bit_Extender bit_extender_1

  assign out_4 = {in_2, in_1};
endmodule

module FA4 (
  input  [3:0] a,
  input  Re,
  output out_3,
  output out_4,
  output out_5,
  output out_6,
  output out_7
);

  wire FA_2_rs, FA_3_rs, FA_4_rs;

  FA1 FA (.Rs(out_3), .a(a[3]), .out_4(out_4), .Re(FA_2_rs));
  FA1 FA_2 (.Rs(FA_2_rs), .a(a[2]), .out_4(out_5), .Re(FA_3_rs));
  FA1 FA_3 (.Rs(FA_3_rs), .a(a[1]), .out_4(out_6), .Re(FA_4_rs));
  FA1 FA_4 (.Rs(FA_4_rs), .a(a[0]), .out_4(out_7), .Re(Re));
endmodule

module FA1 (
  input  a,
  input  Re,
  output Rs,
  output out_4
);

  and and_1 (Rs, Re, a);
  xor xor_1 (out_4, a, Re);
endmodule

module FA8 (
  input  in_1,
  output out_2
);

  wire [7:0] adder_1_out;

  Adder adder_1 (.a(8'h80), .b(8'h8c), .out(adder_1_out), .cin(in_1), .cout(out_2));
  // Probe on adder_1_out
endmodule

module ADDSOUS8bit (
  input  in_1,
  input  [7:0] in_2,
  input  [7:0] in_3,
  output [7:0] out_4
);

  wire [7:0] multiplexer_1_out, not_1_out;

  Multiplexer #(.width(8)) multiplexer_1 (
    .in0(in_2), .in1(not_1_out), .out(multiplexer_1_out), .sel(in_1));  // open: en
  assign not_1_out = ~in_2;  // NOT_Gate not_1, 8 bits wide
  Adder adder_1 (.a(multiplexer_1_out), .b(in_3), .out(out_4), .cin(in_1));  // open: cout

  // Notes on the sheet:
  //   Si 1 on soustrait donc on passe par NON
  //   Si 1 on ajoute la retenu pour faire + 1
endmodule

module ALU_8_bits (
  input  [1:0] in_1,
  input  [7:0] in_2,
  input  [7:0] in_3,
  output out_4,
  output [7:0] out_5
);

  wire and_1_out, not_2_out, not_3_out, not_4_out, not_5_out, not_6_out, not_7_out, not_8_out, not_9_out,
       not_10_out;
  wire [7:0] multiplexer_1_out, not_1_out;

  and and_1 (and_1_out, in_1[1], in_1[0]);
  Multiplexer #(.width(8)) multiplexer_1 (
    .in0(in_2), .in1(not_1_out), .out(multiplexer_1_out), .sel(and_1_out));  // open: en
  assign not_1_out = ~in_2;  // NOT_Gate not_1, 8 bits wide
  not not_2 (not_2_out, in_1[0]);
  Adder adder_1 (.a(multiplexer_1_out), .b(in_3), .out(out_5), .cin(in_1[0]));  // open: cout
  not not_3 (not_3_out, out_5[0]);
  not not_4 (not_4_out, out_5[1]);
  not not_5 (not_5_out, out_5[2]);
  not not_6 (not_6_out, out_5[3]);
  not not_7 (not_7_out, out_5[4]);
  not not_8 (not_8_out, out_5[5]);
  not not_9 (not_9_out, out_5[6]);
  not not_10 (not_10_out, out_5[7]);
  and and_2 (out_4, in_1[1], not_2_out, not_3_out, not_4_out, not_5_out, not_7_out, not_8_out, not_9_out, not_10_out);

  // Notes on the sheet:
  //   Si 1 on soustrait donc on passe par NON
  //   Si 1 on ajoute la retenu pour faire + 1
  //   Test Egalite si a - b = 0
endmodule
